# Fritzing sketch DIY_stay_alive_4_cap_8mm (saved by Fritzing 0.9.3b)
circuit board: 1.5cm x 1.5cm
breadboards: 1

parts:
  C1 = Electrolytic Capacitor [capacitance=1mF package="100 mil [THT, electrolytic]"]
  C2 = Electrolytic Capacitor [capacitance=1mF package="100 mil [THT, electrolytic]"]
  C3 = Electrolytic Capacitor [capacitance=1mF package="100 mil [THT, electrolytic]"]
  C4 = Electrolytic Capacitor [capacitance=1mF voltage=6.3V package="100 mil [THT, electrolytic]"]
  + = Pad [width=2 height=2 connect=center]
  GND = Pad [width=2 height=2 connect=center]
  J2 = female pin header, 2 pins [form="♀ (female)"]
  J1 = female pin header, 4 pins [form="♀ (female)"]

nets:
  N1: C1.-, C4.+
  N2: C1.+, C2.-
  N3: C2.+, C3.-
  N4: C3.+, J2.pin2, J1.pin2, J1.pin4
  N5: C4.-, GND.pad, J2.pin1
  N6: +.pad, J1.pin1, J1.pin3

notes:
  RTSA04-2
