# Fritzing sketch DIY_stay_alive_4_cap_single_row (saved by Fritzing 0.9.3b)
circuit board: 2.43cm x 0.8cm
breadboards: 1

parts:
  C1 = Electrolytic Capacitor [capacitance=1mF package="100 mil [THT, electrolytic]"]
  C2 = Electrolytic Capacitor [capacitance=1mF package="100 mil [THT, electrolytic]"]
  C3 = Electrolytic Capacitor [capacitance=1mF package="100 mil [THT, electrolytic]"]
  C4 = Electrolytic Capacitor [capacitance=1mF voltage=6.3V package="100 mil [THT, electrolytic]"]
  + = Pad [width=2 height=2 connect=center]
  GND = Pad [width=2 height=2 connect=center]
  J1 = female pin header, 4 pins [form="♀ (female)"]
  J2 = female pin header, 1 pin [form="♀ (female)"]
  J3 = female pin header, 1 pin [form="♀ (female)"]

nets:
  N1: C1.-, C4.+
  N2: C1.+, C2.-
  N3: C2.+, C3.-
  N4: C3.+, J1.pin2, J1.pin4, J2.pin1
  N5: C4.-, GND.pad, J3.pin1
  N6: +.pad, J1.pin1, J1.pin3

notes:
  RTSA04-3
