# Fritzing sketch RT_Decoder_3_relay (saved by Fritzing 1.0.0rc)
circuit board: 10cm x 3.5cm
breadboards: 1

parts:
  Nano = Arduino Nano (Rev3.0)
  DCC_in = screw terminal, 2 pins
  D1 = bridge rectifier round [package="round [THT]"]
  IC1 = 6N137 [package="DIP (Dual Inline) [THT]"]
  R1 = Resistor [tolerance=±5% power=0.25 resistance=1k package=THT]
  D2 = Rectifier Diode [part_number=1N4001 package="300 mil [THT]"]
  IC2 = Voltage Regulator [package=to220-igo]
  C1 = Ceramic Capacitor [capacitance=100nF voltage=35V package="100 mil [THT, multilayer]"]
  C2 = Ceramic Capacitor [capacitance=100nF voltage=35V package="100 mil [THT, multilayer]"]
  R2 = Resistor [tolerance=±5% power=0.25 resistance=10k package=THT]
  R3 = Resistor [tolerance=±5% power=0.25 resistance=10k package=THT]
  J1 = female pin header, 8 pins [form="♀ (female)"]
  R4 = Resistor [tolerance=±5% power=0.25 resistance=10k package=THT]
  J2 = female pin header, 2 pins [form="♀ (female)"]
  J3 = female pin header, 8 pins [form="♀ (female)"]
  RLY1 = female pin header, 5 pins [form="♀ (female)"]
  J8 = female pin header, 5 pins [form="♀ (female)"]
  J9 = female pin header, 5 pins [form="♀ (female)"]
  RLY2 = female pin header, 5 pins [form="♀ (female)"]
  J10 = female pin header, 5 pins [form="♀ (female)"]
  RLY3 = female pin header, 5 pins [form="♀ (female)"]
  J4 = female pin header, 2 pins [form="♀ (female)"]
  J5 = female pin header, 2 pins [form="♀ (female)"]
  J6 = female pin header, 2 pins [form="♀ (female)"]
  J7 = female pin header, 2 pins [form="♀ (female)"]

nets:
  GND: Nano.GND, D1.DC-, IC1.pin5, IC2.GND, C1.1, C2.1, J2.pin2
  N1: Nano.D2, IC1.pin6, R3.Pin_0
  N2: Nano.D3, J3.pin1
  N3: Nano.D4, J3.pin2
  N4: Nano.D5, J3.pin3
  N5: Nano.D6, J3.pin4
  N6: Nano.D7, J3.pin5
  N7: Nano.D8, J3.pin6
  N8: Nano.D9, J3.pin7
  N9: Nano.D10, J3.pin8, J10.pin5
  N10: Nano.D11/MOSI, J8.pin5
  N11: Nano.D12/MISO, J9.pin5
  N12: Nano.5V, IC1.pin8, IC2.OUT, C2.0, R2.Pin_1, R3.Pin_1, R4.Pin_0, RLY1.pin5, RLY2.pin5, RLY3.pin5
  N13: Nano.A7, R4.Pin_1, J2.pin1
  N14: Nano.A6, J1.pin1
  N15: Nano.A5, J1.pin2
  N16: Nano.A4, J1.pin3
  N17: Nano.A3, J1.pin4
  N18: Nano.A2, J1.pin5
  N19: Nano.A1, J1.pin6
  N20: Nano.A0, J1.pin7
  N21: Nano.D13/SCK, J1.pin8
  N22: DCC_in.pin1, D1.AC#1, R1.Pin_0
  N23: DCC_in.pin2, D1.AC#0, IC1.pin3, D2.anode
  N24: D1.DC+, IC2.IN, C1.0
  N25: IC1.pin2, R1.Pin_1, D2.cathode
  N26: IC1.pin7, R2.Pin_0
  N27: RLY1.pin1, J8.pin3, J9.pin3, RLY2.pin1, J10.pin3, RLY3.pin1, J4.pin2
  N28: RLY1.pin2, J5.pin1
  N29: RLY1.pin3, J8.pin1, J9.pin1, RLY2.pin3, J10.pin1, RLY3.pin3, J4.pin1
  N30: J8.pin2, J5.pin2
  N31: J9.pin2, J6.pin2
  N32: RLY2.pin2, J6.pin1
  N33: J10.pin2, J7.pin2
  N34: RLY3.pin2, J7.pin1

custom parts:
  6N137: 6N137 opto isolator 8 pin dip.
