# Fritzing sketch RT_Decoder_Marklin_7051 (saved by Fritzing 1.0.0rc)
circuit board: 10cm x 4cm
breadboards: 1

parts:
  Nano = Arduino Nano (Rev3.0)
  DCC_in = screw terminal, 2 pins
  D1 = bridge rectifier round [package="round [THT]"]
  IC1 = 6N137 [package="DIP (Dual Inline) [THT]"]
  R1 = Resistor [tolerance=±5% power=0.25 resistance=1k package=THT]
  D2 = Rectifier Diode [part_number=1N4001 package="300 mil [THT]"]
  IC2 = Voltage Regulator [package=to220-igo]
  C1 = Ceramic Capacitor [capacitance=100nF voltage=35V package="100 mil [THT, multilayer]"]
  C2 = Ceramic Capacitor [capacitance=100nF voltage=35V package="100 mil [THT, multilayer]"]
  R2 = Resistor [tolerance=±5% power=0.25 resistance=10k package=THT]
  R3 = Resistor [tolerance=±5% power=0.25 resistance=10k package=THT]
  R4 = Resistor [tolerance=±5% power=0.25 resistance=10k package=THT]
  J2 = female pin header, 2 pins [form="♀ (female)"]
  RLY2 = DS2Y-5-DC5V [part_number=G6A-234P-ST-US-DC5]
  RLY3 = DS2Y-5-DC5V [part_number=G6A-234P-ST-US-DC5]
  D3 = Diode [package=diode-1n4148]
  D4 = Diode [package=diode-1n4148]
  D5 = Diode [package=diode-1n4148]
  RLY1 = DS2Y-5-DC5V [part_number=G6A-234P-ST-US-DC5]
  J1 = female pin header, 10 pins [form="♀ (female)"]
  J3 = female pin header, 10 pins [form="♀ (female)"]
  J5 = female pin header, 6 pins [form="♀ (female)"]
  J4 = female pin header, 2 pins [form="♀ (female)"]
  Pad1 = Pad [width=2 height=2 connect=center]
  Pad2 = Pad [width=2 height=2 connect=center]
  Pad3 = Pad [width=2 height=2 connect=center]
  Pad4 = Pad [width=2 height=2 connect=center]
  Pad5 = Pad [width=2 height=2 connect=center]
  Pad6 = Pad [width=2 height=2 connect=center]
  C3 = Electrolytic Capacitor [capacitance=22µF voltage=10V package="100 mil [THT, electrolytic]"]
  U1 = Optocoupler [package=THT]
  U2 = Optocoupler [package=THT]
  U3 = Optocoupler [package=THT]
  R5 = Resistor [tolerance=±5% power=0.25W resistance=220 package=THT]
  R6 = Resistor [tolerance=±5% power=0.25W resistance=220 package=THT]
  R7 = Resistor [tolerance=±5% power=0.25W resistance=220 package=THT]

nets:
  GND: Nano.GND, D1.DC-, IC1.pin5, IC2.GND, C1.1, C2.1, J2.pin2, RLY2.16_-, RLY3.16_-, D3.A, D4.A, D5.A, RLY1.16_-, J1.pin10, J3.pin10, C3.-, U1.Pin_2, U2.Pin_2, U3.Pin_2
  N1: Nano.D2, IC1.pin6, R3.Pin_0
  N2: Nano.D3, Nano.5V, IC1.pin8, IC2.OUT, C2.0, R2.Pin_1, R3.Pin_1, R4.Pin_0, J1.pin1, J3.pin1, J3.pin2, C3.+, U1.Pin_5, U2.Pin_5, U3.Pin_5
  N3: Nano.D4, J3.pin3
  N4: Nano.D5, J3.pin4
  N5: Nano.D6, J3.pin5
  N6: Nano.D7, J3.pin6
  N7: Nano.D8, J3.pin7
  N8: Nano.D9, J3.pin8
  N9: Nano.D10, J3.pin9
  N10: Nano.D11/MOSI, J1.pin9, R7.Pin_0
  N11: Nano.D12/MISO, R6.Pin_0
  N12: Nano.A7, R4.Pin_1, J2.pin1
  N13: Nano.A6, J1.pin2
  N14: Nano.A5, J1.pin3
  N15: Nano.A4, J1.pin4
  N16: Nano.A3, J1.pin5
  N17: Nano.A2, J1.pin6
  N18: Nano.A1, J1.pin7
  N19: Nano.A0, J1.pin8
  N20: Nano.D13/SCK, R5.Pin_0
  N21: DCC_in.pin1, D1.AC#1, R1.Pin_0
  N22: DCC_in.pin2, D1.AC#0, IC1.pin3, D2.anode
  N23: D1.DC+, IC2.IN, C1.0
  N24: IC1.pin2, R1.Pin_1, D2.cathode
  N25: IC1.pin7, R2.Pin_0
  N26: RLY2.8_N.O., RLY2.11_N.C., J5.pin4
  N27: RLY2.6_N.C., RLY2.9_N.O., J5.pin3, Pad3.pad, Pad4.pad
  N28: RLY2.4_COM, RLY3.4_COM, RLY1.4_COM, J4.pin2
  N29: RLY2.1_+, D4.C, U2.Pin_4
  N30: RLY2.13_COM, RLY3.13_COM, RLY1.13_COM, J4.pin1
  N31: RLY3.8_N.O., RLY3.11_N.C., J5.pin6
  N32: RLY3.6_N.C., RLY3.9_N.O., J5.pin5, Pad5.pad, Pad6.pad
  N33: RLY3.1_+, D5.C, U3.Pin_4
  N34: D3.C, RLY1.1_+, U1.Pin_4
  N35: RLY1.8_N.O., RLY1.11_N.C., J5.pin2
  N36: RLY1.6_N.C., RLY1.9_N.O., J5.pin1, Pad1.pad, Pad2.pad
  N37: U1.Pin_1, R5.Pin_1
  N38: U2.Pin_1, R6.Pin_1
  N39: U3.Pin_1, R7.Pin_1

notes:
  gnd
  +
  1
  2
  3
  4
  5
  6
  7
  8
  9
  10
  11
  12
  13
  14
  15
  16
  RT 3 RLY 3

custom parts:
  6N137: 6N137 opto isolator 8 pin dip.
