# Fritzing sketch led_high_low (saved by Fritzing 1.0.0rc)
breadboards: 1

parts:
  R1 = Resistor [tolerance=±5% power=0.25W resistance=220 package=THT]
  LED1 = LED - 5mm [color="Red (633nm)" current=0.030A package="5 mm [THT]"]
  R2 = Resistor [tolerance=±5% power=0.25W resistance=220 package=THT]
  LED2 = LED - 5mm [color="Red (633nm)" current=0.030A package="5 mm [THT]"]

nets:
  +: R1.Pin_0
  S: LED1.cathode, R2.Pin_0
  G: LED2.cathode

notes:
  High Output
  Low Output
