# Fritzing sketch RT_Pulse_8_decoder (saved by Fritzing 0.9.3b)
circuit board: 8.5cm x 10cm
breadboards: 1

parts:
  Nano = Arduino Nano (Rev3.0)
  -2 = female pin header, 2 pins [form="♀ (female)"]
  BR1 = female alternating pin header, 2 pins [form="♀ (female)"]
  C2 = Electrolytic Capacitor [capacitance=22µF voltage=20V package="100 mil [THT, electrolytic]"]
  C1 = Tantalum Capacitor [capacitance=1µF voltage=20V package="100 mil [THT, tantalum]"]
  C3 = Tantalum Capacitor [capacitance=1µF voltage=20V package="100 mil [THT, tantalum]"]
  IC2 = IC, DIP package, 8 pins [chip_label=IC part_number=6N137]
  R1 = Resistor [tolerance=±5% resistance=1k power=0.25 package=THT]
  D2 = Rectifier Diode [part_number=1N4001 package="300 mil [THT]"]
  C4 = Ceramic Capacitor [capacitance=100nF voltage=20V package="100 mil [THT, multilayer]"]
  R2 = Resistor [tolerance=±5% resistance=10k power=0.25 package=THT]
  R3 = Resistor [tolerance=±5% resistance=10k power=0.25 package=THT]
  U1 = Voltage Regulator - 5V [package="TO220 [THT]"]
  J18 = screw terminal, 2 pins
  ZD1 = Zener Diode [part_number=1N4749A breakdown_voltage=24V package="300 mil [THT]"]
  J20 = female pin header, 1 pin [form="♀ (female)"]
  J21 = screw terminal, 2 pins
  -3 = female pin header, 2 pins [form="♀ (female)"]
  BR2 = female alternating pin header, 2 pins [form="♀ (female)"]
  R8 = Resistor [tolerance=±5% resistance=2.2k power=0.25 package=THT]
  R9 = Resistor [tolerance=±5% resistance=2.2k power=0.25 package=THT]
  R10 = Resistor [tolerance=±5% resistance=2.2k power=0.25 package=THT]
  Q1 = npn-Powertransistor [part_number=TIP41C package="TO220 [THT]"]
  C5 = Electrolytic Capacitor [capacitance=410µ voltage=35V part_number=10000µF package="300 mil [THT, electrolytic]"]
  D1 = Rectifier Diode [part_number=1N4007 package="300 mil [THT]"]
  1 = female pin header, 3 pins [form="♀ (female)"]
  2 = female pin header, 3 pins [form="♀ (female)"]
  3 = female pin header, 3 pins [form="♀ (female)"]
  4 = female pin header, 3 pins [form="♀ (female)"]
  5 = female pin header, 3 pins [form="♀ (female)"]
  6 = female pin header, 3 pins [form="♀ (female)"]
  7 = female pin header, 3 pins [form="♀ (female)"]
  8 = female pin header, 3 pins [form="♀ (female)"]
  ULN2 = Darlington Driver [part_number=ULN2803 package=dil18]
  ULN1 = Darlington Driver [part_number=ULN2803 package=dil18]
  LED1 = LED - 3mm [color="Blue (505nm)" current=0.030 package="3 mm [THT]"]
  R11 = Resistor [tolerance=±5% power=0.25 resistance=2.2k package=THT]
  J22 = female pin header, 1 pin [form="♀ (female)"]
  J23 = female pin header, 1 pin [form="♀ (female)"]
  J24 = female pin header, 1 pin [form="♀ (female)"]
  J25 = female pin header, 1 pin [form="♀ (female)"]
  J26 = female pin header, 2 pins [form="♀ (female)"]
  R12 = Resistor [tolerance=±5% power=0.25 resistance=10k package=THT]
  Learn = female pin header, 2 pins [form="♀ (female)"]

nets:
  GND: Nano.GND, -2.pin1, C2.-, C1.-, C3.-, IC2.pin5, U1.GND, ZD1.anode, -3.pin1, C5.-, ULN2.9, ULN1.9, R11.Pin_0, J24.pin1, J25.pin1, R12.Pin_0
  N1: Nano.D2, IC2.pin6, R2.Pin_0
  N2: Nano.D3, ULN2.8
  N3: Nano.D4, ULN2.7
  N4: Nano.D5, ULN2.6
  N5: Nano.D6, ULN2.5
  N6: Nano.D7, ULN2.4
  N7: Nano.D8, ULN2.3
  N8: Nano.D9, ULN2.2
  N9: Nano.D10, ULN2.1
  N10: Nano.D11/MOSI, ULN1.8
  N11: Nano.D12/MISO, ULN1.7
  N12: Nano.5V, C2.+, C3.+, IC2.pin8, R2.Pin_1, R3.Pin_1, U1.output_voltage, Learn.pin1
  N13: Nano.A6, R12.Pin_1, Learn.pin2
  N14: Nano.A5, ULN1.1
  N15: Nano.A4, ULN1.2
  N16: Nano.A3, ULN1.3
  N17: Nano.A2, ULN1.4
  N18: Nano.A0, ULN1.5
  N19: Nano.D13/SCK, ULN1.6
  N20: -2.pin2, IC2.pin3, D2.anode, C4.1, J18.pin2
  N21: BR1.pin1, R1.Pin_0, J18.pin1
  N22: BR1.pin2, C1.+, U1.input_voltage
  N23: IC2.pin2, R1.Pin_1, D2.cathode, C4.0
  N24: IC2.pin7, R3.Pin_0
  N25: ZD1.cathode, J20.pin1, Q1.emitter, C5.+, D1.anode
  N26: J21.pin1, BR2.pin1
  N27: J21.pin2, -3.pin2
  N28: BR2.pin2, R8.Pin_1, R9.Pin_1, R10.Pin_1, J22.pin1, J26.pin2
  N29: R8.Pin_0, R9.Pin_0, R10.Pin_0, Q1.base, D1.cathode, 1.pin1, 2.pin1, 3.pin1, 4.pin1, 5.pin1, 6.pin1, 7.pin1, 8.pin1, ULN2.10, ULN1.10, LED1.anode
  N30: Q1.collector, J23.pin1, J26.pin1
  N31: 1.pin2, ULN2.12
  N32: 1.pin3, ULN2.11
  N33: 2.pin2, ULN2.14
  N34: 2.pin3, ULN2.13
  N35: 3.pin2, ULN2.16
  N36: 3.pin3, ULN2.15
  N37: 4.pin2, ULN2.18
  N38: 4.pin3, ULN2.17
  N39: 5.pin2, ULN1.12
  N40: 5.pin3, ULN1.11
  N41: 6.pin2, ULN1.14
  N42: 6.pin3, ULN1.13
  N43: 7.pin2, ULN1.16
  N44: 7.pin3, ULN1.15
  N45: 8.pin2, ULN1.18
  N46: 8.pin3, ULN1.17
  N47: LED1.cathode, R11.Pin_1

notes:
  1
  RT DCC TD8 2
  +
  DCC In
  B
  C
  T
  Input
  Base turnout address
