# Fritzing sketch RT_Solenoid_turnout_driver_jst_v2_SM (saved by Fritzing 1.0.0rc)
circuit board: 8.5cm x 10cm
breadboards: 1

parts:
  3 = female pin header, 3 pins [form="♀ (female)"]
  2 = female pin header, 3 pins [form="♀ (female)"]
  1 = female pin header, 3 pins [form="♀ (female)"]
  0 = female pin header, 3 pins [form="♀ (female)"]
  3_2 = female pin header, 3 pins [form="♀ (female)"]
  2_2 = female pin header, 3 pins [form="♀ (female)"]
  1_2 = female pin header, 3 pins [form="♀ (female)"]
  ULN1 = Darlington Driver [package=dil18]
  ULN2 = Darlington Driver [package=dil18]
  0_2 = female pin header, 3 pins [form="♀ (female)"]
  J14 = male pin header, 2 pins [form="♂ (male)"]
  J12 = male pin header, 2 pins [form="♂ (male)"]
  J13 = male pin header, 2 pins [form="♂ (male)"]
  J15 = male pin header, 4 pins [form="♂ (male)"]
  J16 = female pin header, 2 pins [form="♀ (female)"]
  Q1 = npn-Powertransistor [package="TO220 [THT]"]
  C2 = Electrolytic Capacitor [capacitance=470µF voltage=35V part_number=4700µF package="300 mil [THT, electrolytic]"]
  C1 = Electrolytic Capacitor [capacitance=470µF voltage=35V part_number=4700µF package="300 mil [THT, electrolytic]"]
  J17 = screw terminal, 2 pins
  J18 = Qwic 1mm JST connector [package=SMD]
  R2 = Resistor [tolerance=±5% resistance=10k power=0.25 package="0805 [SMD]"]
  R3 = Resistor [tolerance=±5% resistance=10k power=0.25 package="0805 [SMD]"]
  R4 = Resistor [tolerance=±5% resistance=10k power=0.25 package="0805 [SMD]"]
  R1 = Resistor [tolerance=±5% resistance=470 power=0.25 package="0805 [SMD]"]
  LED1 = smd LED [color="Red (633nm)" current=0.030 package="0805 [SMD]"]
  R5 = Resistor [tolerance=±5% resistance=820 power=0.25 package="0805 [SMD]"]
  R6 = Resistor [tolerance=±5% resistance=820 power=0.25 package="0805 [SMD]"]
  R7 = Resistor [tolerance=±5% resistance=820 power=0.25 package="0805 [SMD]"]
  R8 = Resistor [tolerance=±5% resistance=1k power=0.25 package="0805 [SMD]"]
  LED2 = smd LED [color="Red (633nm)" current=0.030 package="0805 [SMD]"]
  BR1 = bridge rectifier TO-269AA [package="TO-269AA [SMD]"]
  D1 = Rectifier Diode [part_number=1N4007 package="300 mil [THT]"]
  MCP23017 = SO-28W [chip_label=IC package=SO(w)]
  J19 = Qwic 1mm JST connector [package=SMD]

nets:
  N1: 3.pin1, 2.pin1, 1.pin1, 0.pin1, 3_2.pin1, 2_2.pin1, 1_2.pin1, ULN1.10, ULN2.10, 0_2.pin1, Q1.base, R5.Pin_0, R6.Pin_0, R7.Pin_0, D1.cathode
  N2: 3.pin2, ULN1.18
  N3: 3.pin3, ULN1.17
  N4: 2.pin2, ULN1.16
  N5: 2.pin3, ULN1.15
  N6: 1.pin2, ULN1.14
  N7: 1.pin3, ULN1.13
  N8: 0.pin2, ULN1.12
  N9: 0.pin3, ULN1.11
  N10: 3_2.pin2, ULN2.18
  N11: 3_2.pin3, ULN2.17
  N12: 2_2.pin2, ULN2.16
  N13: 2_2.pin3, ULN2.15
  N14: 1_2.pin2, ULN2.14
  N15: 1_2.pin3, ULN2.13
  N16: ULN1.1, MCP23017.8
  N17: ULN1.2, MCP23017.7
  N18: ULN1.3, MCP23017.6
  N19: ULN1.4, MCP23017.5
  N20: ULN1.5, MCP23017.4
  N21: ULN1.6, MCP23017.3
  N22: ULN1.7, MCP23017.2
  N23: ULN1.8, MCP23017.1
  N24: ULN1.9, ULN2.9, J15.pin1, J16.pin1, J16.pin2, C2.-, C1.-, J18.pin_1, R2.Pin_0, R3.Pin_0, R4.Pin_0, LED1.cathode, LED2.cathode, BR1.DC-, MCP23017.10, J19.pin_1
  N25: ULN2.1, MCP23017.28
  N26: ULN2.2, MCP23017.27
  N27: ULN2.3, MCP23017.26
  N28: ULN2.4, MCP23017.25
  N29: ULN2.5, MCP23017.24
  N30: ULN2.6, MCP23017.23
  N31: ULN2.7, MCP23017.22
  N32: ULN2.8, MCP23017.21
  N33: ULN2.11, 0_2.pin3
  N34: ULN2.12, 0_2.pin2
  N35: J14.pin1, J12.pin1, J13.pin1, J15.pin2, J18.pin_2, R1.Pin_0, MCP23017.9, J19.pin_2
  N36: J14.pin2, R2.Pin_1, MCP23017.15
  N37: J12.pin2, R4.Pin_1, MCP23017.17
  N38: J13.pin2, R3.Pin_1, MCP23017.16
  N39: J15.pin3, J18.pin_3, MCP23017.13, J19.pin_3
  N40: J15.pin4, J18.pin_4, MCP23017.12, J19.pin_4
  N41: Q1.collector, R5.Pin_1, R6.Pin_1, R7.Pin_1, BR1.DC+
  N42: Q1.emitter, C2.+, C1.+, R8.Pin_1, D1.anode
  N43: J17.pin1, BR1.AC#0
  N44: J17.pin2, BR1.AC#1
  N45: R1.Pin_1, LED1.anode
  N46: R8.Pin_0, LED2.anode

notes:
  VCC
  GND
  SCL
  SDA
  0
  1
  2
  Input
  +
  RT CDUP 4 SMT
  I2C
  B
  C
  E
  <- ADDRESS ->
  T

custom parts:
  Qwic 1mm JST connector: Sparkfun PRT-14417 Qwiic JST Connector - SMD 4-pin (Horizontal) connector SMD.
