# Fritzing sketch RT_stay_alive_4_cap (saved by Fritzing 1.0.0rc)
circuit board: 1.3cm x 1.3cm
breadboards: 1

parts:
  C1 = Electrolytic Capacitor [capacitance=1mF voltage=35V package="100 mil [THT, electrolytic]"]
  C2 = Electrolytic Capacitor [capacitance=1mF package="100 mil [THT, electrolytic]"]
  C3 = Electrolytic Capacitor [capacitance=1mF voltage=35V package="100 mil [THT, electrolytic]"]
  C4 = Electrolytic Capacitor [capacitance=1mF voltage=6.3V package="100 mil [THT, electrolytic]"]
  + = Pad [width=1.5 height=1.5 connect=center]
  GND = Pad [width=1.5 height=1.5 connect=center]
  J1 = female pin header, 4 pins [form="♀ (female)"]
  J2 = female pin header, 1 pin [form="♀ (female)"]
  J3 = female pin header, 1 pin [form="♀ (female)"]

nets:
  N1: C1.-, C4.+
  N2: C1.+, C2.-
  N3: C2.+, C3.-
  N4: C3.+, J1.pin2, J1.pin4, J3.pin1
  GND: C4.-, GND.pad, J2.pin1
  +: +.pad, J1.pin1, J1.pin3

notes:
  RTSA04-2
