# Fritzing sketch RT_stay_alive_8_cap (saved by Fritzing 0.9.3b)
circuit board: 2.8cm x 1.3cm
breadboards: 1

parts:
  C1 = Electrolytic Capacitor [capacitance=1mF package="100 mil [THT, electrolytic]"]
  C2 = Electrolytic Capacitor [capacitance=1mF package="100 mil [THT, electrolytic]"]
  C3 = Electrolytic Capacitor [capacitance=1mF package="100 mil [THT, electrolytic]"]
  C4 = Electrolytic Capacitor [capacitance=1mF voltage=6.3V package="100 mil [THT, electrolytic]"]
  + = Pad [width=1.5 height=1.5 connect=center]
  GND = Pad [width=1.5 height=1.5 connect=north]
  C5 = Electrolytic Capacitor [capacitance=1mF package="100 mil [THT, electrolytic]"]
  C6 = Electrolytic Capacitor [capacitance=1mF package="100 mil [THT, electrolytic]"]
  C7 = Electrolytic Capacitor [capacitance=1mF package="100 mil [THT, electrolytic]"]
  C8 = Electrolytic Capacitor [capacitance=1mF package="100 mil [THT, electrolytic]"]
  J1 = female pin header, 4 pins [form="♀ (female)"]
  J2 = female pin header, 2 pins [form="♀ (female)"]

nets:
  N1: C1.-, C6.+
  N2: C1.+, C2.-
  N3: C2.+, C3.-
  N4: C3.+, J1.pin2, J1.pin4, J2.pin2
  N5: C4.-, GND.pad, J2.pin1
  N6: C4.+, C5.-
  N7: +.pad, J1.pin1, J1.pin3
  N8: C5.+, C7.-
  N9: C6.-, C8.+
  N10: C7.+, C8.-

notes:
  RT SA 06
